# Fritzing sketch LightSwitch (saved by Fritzing 0.9.3b)
breadboards: 1

parts:
  Part1 = Arduino Nano (Rev3.0)
  S1 = Pushbutton [package="[SMD]"]
  R1 = Resistor [tolerance=±5% resistance=100 package=THT]
  Relay_5V1 = Keyes Relay [package=THT]
  HC-7 = Bluetooth HC-05 Macho
  BULB1 = Incandescent light bulb small [package="bulb sm"]
  Part3 = Lilypad Battery Connect
  Part4 = Lilypad Battery Connect

nets:
  GND: Part1.GND, R1.Pin_1, Relay_5V1.ground, HC-7.GND, Part4.+
  N1: Part1.D3, S1.Pin_1, S1.Pin_2, R1.Pin_0
  N2: Part1.D4, Relay_5V1.signal
  N3: Part1.D8, HC-7.TXD
  N4: Part1.D10, HC-7.RXD
  5V: Part1.5V, S1.Pin_3, S1.Pin_4, Relay_5V1.power, HC-7.VCC, Part4.-
  N5: Relay_5V1.C, Part3.-
  N6: Relay_5V1.NO, BULB1.2
  N7: BULB1.1, Part3.+

notes:
  220v ac
  These 2 black wires can be at your wall switch or, you can just use wall plug
  5v dc

custom parts:
  Keyes Relay: The Keyes 5V relay module is suitable for SCM development, home appliance control. It uses a 5V~12V TIL control signal which can control DC / AC signal.
